# Fritzing sketch Wiring (saved by Fritzing 0.9.3b)

parts:
  Composant1 = Arduino Uno (Rev3) - ICSP
  J1 = Basic Servo
  J2 = Basic Servo
  J3 = Basic Servo
  Power_plug1 = Power plug  # not connected

nets:
  GND: Composant1.GND, J2.gnd
  N1: Composant1.D3_PWM, J1.pulse
  N2: Composant1.D5_PWM, J2.pulse
  N3: Composant1.D6_PWM, J3.pulse

notes:
  Servo 1
  Servo 2
  Servo 3
  To 5V external power supply
